# Fritzing sketch light_levels (saved by Fritzing 0.9.5d)
breadboards: 1

parts:
  LED1 = smd LED [color="Red (633nm)" package="0603 [SMD]"]
  LED2 = smd LED [color="Red (633nm)" package="0603 [SMD]"]
  LED3 = smd LED [color="Red (633nm)" package="0603 [SMD]"]
  LED4 = smd LED [color="Red (633nm)" package="0603 [SMD]"]
  LED5 = smd LED [color="Red (633nm)" package="0603 [SMD]"]
  WeMos_D1_Mini1 = WeMos D1 Mini
  R1 = Resistor [tolerance=±5% resistance=220 package="1206 [SMD]"]
  R2 = Resistor [tolerance=±5% resistance=220 package="1206 [SMD]"]
  R3 = Resistor [tolerance=±5% resistance=220 package="1206 [SMD]"]
  R4 = Resistor [tolerance=±5% resistance=220 package="1206 [SMD]"]
  R5 = Resistor [tolerance=±5% resistance=220 package="1206 [SMD]"]
  e-radionica_com1 = LM393 LDR breakout [part_number=100027]

nets:
  N1: LED1.cathode, R1.Pin_0
  N2: LED1.anode, WeMos_D1_Mini1.D8
  N3: LED2.cathode, R2.Pin_0
  N4: LED2.anode, WeMos_D1_Mini1.D7
  N5: LED3.cathode, R3.Pin_0
  N6: LED3.anode, WeMos_D1_Mini1.D6
  N7: LED4.cathode, R4.Pin_0
  N8: LED4.anode, WeMos_D1_Mini1.D5
  N9: LED5.cathode, R5.Pin_0
  N10: LED5.anode, WeMos_D1_Mini1.D0
  5V: WeMos_D1_Mini1.5V, e-radionica_com1.VCC
  N11: WeMos_D1_Mini1.A0, e-radionica_com1.AO
  N12: WeMos_D1_Mini1.G, R1.Pin_1, R2.Pin_1, R3.Pin_1, R4.Pin_1, R5.Pin_1, e-radionica_com1.GND

custom parts:
  WeMos D1 Mini: The D1 mini is a mini wifi board based on ESP-8266EX.
